// Logisim project Rom_based.circ as structural Verilog: 1 circuit, main circuit main
module main (
  input  [6:0] in_1
);

  wire and_1_out, and_2_out, and_3_out, and_4_out, and_5_out, clock_1_out, comparator_1_eq, comparator_1_lt,
       comparator_2_eq, comparator_2_gt, comparator_2_lt, comparator_3_eq, comparator_3_gt, comparator_3_lt,
       comparator_4_eq, comparator_4_gt, comparator_4_lt, comparator_5_eq, comparator_5_gt, comparator_5_lt,
       comparator_6_eq, comparator_6_gt, or_1_out, or_2_out, or_3_out, or_4_out, or_5_out;
  wire [3:0] rom_1_data;
  wire [7:0] register_1_q;
  wire [24:0] rom_2_data;

  Comparator #(.width(7), .mode("unsigned")) comparator_1 (
    .a(in_1), .b(7'b1100100), .eq(comparator_1_eq), .lt(comparator_1_lt));  // open: gt
  Comparator #(.width(7), .mode("unsigned")) comparator_2 (
    .a(in_1), .b(7'b1010000), .gt(comparator_2_gt), .eq(comparator_2_eq), .lt(comparator_2_lt));
  Comparator #(.width(7), .mode("unsigned")) comparator_3 (
    .a(in_1), .b(7'b0111100), .gt(comparator_3_gt), .eq(comparator_3_eq), .lt(comparator_3_lt));
  Comparator #(.width(7), .mode("unsigned")) comparator_4 (
    .a(in_1), .b(7'b0101000), .gt(comparator_4_gt), .eq(comparator_4_eq), .lt(comparator_4_lt));
  Comparator #(.width(7), .mode("unsigned")) comparator_5 (
    .a(in_1), .b(7'b0010100), .gt(comparator_5_gt), .eq(comparator_5_eq), .lt(comparator_5_lt));
  Comparator #(.width(7), .mode("unsigned")) comparator_6 (
    .a(in_1), .b({7{1'b0}}), .gt(comparator_6_gt), .eq(comparator_6_eq));  // open: lt
  or or_1 (or_1_out, comparator_1_eq, comparator_1_lt);
  or or_2 (or_2_out, comparator_4_gt, comparator_4_eq);
  or or_3 (or_3_out, comparator_2_gt, comparator_2_eq);
  or or_4 (or_4_out, comparator_3_gt, comparator_3_eq);
  or or_5 (or_5_out, comparator_5_gt, comparator_5_eq);
  and and_1 (and_1_out, or_1_out, or_3_out);
  and and_2 (and_2_out, comparator_2_lt, or_4_out);
  and and_3 (and_3_out, comparator_3_lt, or_2_out);
  and and_4 (and_4_out, comparator_4_lt, or_5_out);
  and and_5 (and_5_out, comparator_5_lt, comparator_6_gt);
  Priority_Encoder #(.select(4), .disabled(0)) priority_encoder_1 (
    .in0(comparator_6_eq), .in1(and_5_out), .in2(and_4_out), .in3(and_3_out), .in4(and_2_out),
    .in5(and_1_out), .out(register_1_q[7:4]));  // open: in6, in7, in8, in9, in10, in11, in12, in13, in14, in15, gs, en_out, en_in
  ROM #(.dataWidth(4)) rom_1 (.addr(register_1_q), .data(rom_1_data));  // open: sel
  Clock clock_1 (.out(clock_1_out));
  Register #(.width(4)) register_1 (.D(rom_1_data), .Q(register_1_q[3:0]), .clk(clock_1_out));  // open: en, clr
  ROM #(.addrWidth(4), .dataWidth(25)) rom_2 (.addr(register_1_q[3:0]), .data(rom_2_data));  // open: sel
  DotMatrix #(.matrixrows(5)) dotmatrix_1 (
    .col0(rom_2_data[4:0]), .col1(rom_2_data[9:5]), .col2(rom_2_data[14:10]), .col3(rom_2_data[19:15]),
    .col4(rom_2_data[24:20]));

  // Notes on the sheet:
  //   2-bit Signal Input
  //   SS = 0
  //   contents of rom_1 (hex, n*v repeats v):
  //   6 5*0 7 8 9 a 6*0 1 5*0 11*1 2 4*0 10*2 1 2 3 0 0 0 10*3 1 2 3 4 0 0 10*4 1 2 3 4 5 0 10*5
  //   contents of rom_2 (hex, n*v repeats v):
  //   0 1 61 1c61 79c61 1f79c61 1000 729c0 1f8c63f 729c0 1000
endmodule
